# Fritzing sketch [F3] Circuit  diagram_Arduino code (saved by Fritzing 0.9.3b)
circuit board: 12cm x 7cm
breadboards: 1

parts:
  Q2 = Basic FET P-Channel [part_number=IRLZ44N package="TO220 [THT]"]
  Q3 = Basic FET P-Channel [part_number=IRLZ44N package="TO220 [THT]"]
  Arduino_Nano = Arduino Nano (Rev3.0)
  R1 = Resistor [tolerance=±1% power=0.25 resistance=10k package=THT]
  R2 = Resistor [tolerance=±1% power=0.25 resistance=10k package=THT]
  R3 = Resistor [tolerance=±1% power=0.25 resistance=10k package=THT]
  LCD = female pin header, 4 pins [form="♀ (female)"]
  Thermistors = female pin header, 4 pins [form="♀ (female)"]
  D1 = Rectifier Diode [part_number=1N4001 package="300 mil [THT]"]
  Rth(10k) = Resistor [tolerance=±0.1% power=0.25 resistance=10k package=THT]
  Rth(10k)_2 = Resistor [tolerance=±0.1% power=0.25 resistance=10k package=THT]
  V_ext_12V = Camdenboss CTB0158-2 [part_number=CTB0158-2 package=THT]
  S/W = Toggle Switch [package=THT]
  MCP3550 = SO08 [chip_label=IC package=SO]
  LED1 = LED SMD 1206 - Top View [color="Red (633nm)" current=0.030 package="1206 [SMD] Top"]
  PH_LED = LED SMD 1206 - Top View [color="Red (633nm)" current=30mA package="1206 [SMD] Top"]
  Bat_12V = Power plug
  PW_S/W = female pin header, 3 pins [form="♀ (female)"]
  C1 = Ceramic Capacitor [capacitance=100nF package="100 mil [THT, multilayer]"]
  R8 = Resistor [tolerance=±1% power=0.25 resistance=10k package=THT]
  Vin<9V = female pin header, 2 pins [form="♀ (female)"]
  C2 = Electrolytic Capacitor [capacitance=1mF part_number="1000uF 50V" package="200 mil [THT, electrolytic]"]
  C3 = Electrolytic Capacitor [capacitance=1µF package="200 mil [THT, electrolytic]"]
  p3 = female pin header, 8 pins [form="♀ (female)"]  # not connected
  p4 = female pin header, 8 pins [form="♀ (female)"]  # not connected
  p5 = female pin header, 8 pins [form="♀ (female)"]  # not connected
  p6 = female pin header, 8 pins [form="♀ (female)"]  # not connected
  p7 = female pin header, 10 pins [form="♀ (female)"]
  p8 = female pin header, 10 pins [form="♀ (female)"]
  p9 = female pin header, 10 pins [form="♀ (female)"]
  Mosfet_Vout = Camdenboss CTB0158-6 [part_number=CTB0158-6 package=THT]
  PH_S/W = female pin header, 6 pins [form="♀ (female)"]
  R9 = Resistor [tolerance=±5% resistance=330 power=0.25 package="0805 [SMD]"]
  R7 = Resistor [tolerance=±5% resistance=220 power=0.25 package="0805 [SMD]"]
  J1 = female pin header, 2 pins [form="♀ (female)"]
  H-FAN = female pin header, 4 pins [form="♀ (female)"]
  Q1 = Basic FET P-Channel [part_number=IRLZ44N package="TO220 [THT]"]
  P = female pin header, 1 pin [form="♀ (female)"]
  D2 = Rectifier Diode [part_number=1N4007 package="300 mil [THT]"]
  p1 = female pin header, 4 pins [form="♀ (female)"]
  p2 = female pin header, 4 pins [form="♀ (female)"]  # not connected

nets:
  N1: Q2.gate, Arduino_Nano.D5, R2.Pin_0
  N2: Q2.drain, Mosfet_Vout.pin3
  GND: Q2.source, Q3.source, Arduino_Nano.GND, R1.Pin_1, R2.Pin_1, R3.Pin_1, LCD.pin4, Thermistors.pin1, Thermistors.pin3, V_ext_12V.pin1, MCP3550.3, MCP3550.4, Bat_12V.GND, C1.0, R8.Pin_0, Vin<9V.pin2, C2.-, C3.-, p7.pin5, p8.pin5, p9.pin1, p9.pin2, p9.pin3, p9.pin4, p9.pin5, p9.pin6, p9.pin7, p9.pin8, p9.pin9, p9.pin10, R9.Pin_0, R7.Pin_1, H-FAN.pin4, Q1.source, D2.anode, p1.pin1
  N3: Q3.gate, Arduino_Nano.D6, R3.Pin_0
  N4: Q3.drain, Mosfet_Vout.pin1
  N5: Arduino_Nano.D2, C1.1, R8.Pin_1, PH_S/W.pin5, J1.pin1
  N6: Arduino_Nano.D3, H-FAN.pin1
  N7: Arduino_Nano.D4, LED1.anode, PH_S/W.pin1
  N8: Arduino_Nano.D7, p7.pin3
  N9: Arduino_Nano.D8, p7.pin4
  N10: Arduino_Nano.D10, MCP3550.7
  N11: Arduino_Nano.D11/MOSI, R1.Pin_0, Q1.gate
  N12: Arduino_Nano.D12/MISO, MCP3550.6
  N13: Arduino_Nano.VIN, S/W.L2, C3.+
  N14: Arduino_Nano.5V, LCD.pin3, Rth(10k).Pin_0, Rth(10k)_2.Pin_0, MCP3550.1, MCP3550.8, p7.pin1, PH_S/W.pin6, J1.pin2
  N15: Arduino_Nano.A5, LCD.pin1
  N16: Arduino_Nano.A4, LCD.pin2
  N17: Arduino_Nano.A3, PH_LED.anode, PH_S/W.pin3
  N18: Arduino_Nano.A2, p7.pin2
  N19: Arduino_Nano.A0, Thermistors.pin4, Rth(10k).Pin_1
  N20: Arduino_Nano.D13/SCK, MCP3550.5
  N21: Thermistors.pin2, Rth(10k)_2.Pin_1, MCP3550.2
  N22: D1.cathode, PW_S/W.pin3, C2.+, Mosfet_Vout.pin2, Mosfet_Vout.pin4, Mosfet_Vout.pin6, H-FAN.pin3, D2.cathode
  N23: D1.anode, Mosfet_Vout.pin5, Q1.drain
  N24: V_ext_12V.pin2, Bat_12V.VCC, PW_S/W.pin1, PW_S/W.pin2
  N25: S/W.COM, Vin<9V.pin1, P.pin1
  N26: LED1.cathode, PH_S/W.pin2, R9.Pin_1
  N27: PH_LED.cathode, PH_S/W.pin4, R7.Pin_0
  N28: Mosfet_Vout.terminal_3, Mosfet_Vout.terminal_4, Mosfet_Vout.terminal_5

notes:
  Bio-PCR, Unit 15s
  BIL, Sogang Univ.
  Heater
  L-FAN
  +  -
  A0 1 2 3 4 5 6 7
  Vin
  5V
  A5 A4 V G
  GND
  Th_ADC/A0
  DC B A 9 8 7 6 5 4 3 2
  Warning!
  D4
  A3
  D2
  Ver. 3.0 (2023)
  D11
  D5
  D6
  G Vs S P
  Peltier
  w/o C3
  Encorder
  G  s1 s2 s/w  V
  s1 s2

custom parts:
  LED SMD 1206 - Top View: A generic SMD LED (~1.8V)

// code stored in the sketch: Bio_PCR_Unit15s_Pel3_B_v04.ino
// Program for PCR Unit15_B ===================================================================
// Model: Unit15_Pel3_B_Pub_01, Heat sink: Al_03 
// This is PID control program for PCR thermal cycle with 4 ch. thermal loops.
// - Temperature measurement using a NTC thermistor
// - Battery: 12.8 V ~ 29.2 V, MOSFET IRLZ44N
// - Stepper motor driver chip: A4988 only for Rot.-PCR      
// - Heating: Two heaters (Upper/Lower serial connection)
// - Cooling: Peltier element (Cooling mode only), H-fan and L-fan 
// - Max. capacity: Four-Ch.'s control
//
//       Biological Interfaces Laboratory, Sogang University in Seoul, Korea  
//                  By Oh-Sun Kwon  (Oct. 20, 2024) 
//                                  
// ref: https://www.circuitbasics.com/arduino-thermistor-temperature-sensor-tutorial/
////////////////////////////////////////////////////////////////////////////////////////////////
//
//  It is set to PCR thermal cycle in 3-phases of temperature.
//
////Key variable paprameters: //////////////////////////////////////////////////////////////////
// 
// Tcr: operating indicator blue LED, set it usually slightly over room temperature (Ex.: 26 oC)  
// Time: tt1 (1st long heating), t1 (heating ramp), t2(denaturation), 
//        t3 (cooling ramp), t4 (annealing and enlogation)
//        Ex.) 50, 40, 5, 35, 25 (Note: Temporary it is not real time (s) but looping number (n)        
// mx: Total cycle number: Ex.) mx = 40
// Setpoint0 (Ch. 1: Heater), 1 (Ch. 2: L-fan), 2 (Ch. 3: H-fan), 3 (Ch. 4: Peltier cooling)
//        Ex.) sp0 = 93 oC, sp1 = 90 oC, sp2 = 56 oC  
// PID parameters:  Kp0, Ki0, Kd0, Output0 
// 
//  
///////////////////////////////////////////////////////////////////////////////////////////////

///////////////////////////////////////////////////////////////////////////////////////////////
//=============================================================================================

#include <stdint.h>
#include <Wire.h>                       
#include <LiquidCrystal_I2C.h>
#include <Time.h>
#include <PID_v1.h>
#include <PWM.h>
#include <Bounce2.h>

// pin asignment
//PWM = pin (~5,~6: Timer0=1kHz), (~9,~10: Timer1=500Hz), (~3,~11: Timer2=500Hz): Only 6 pins are possible for PWM mode. Change D3 for 25kHz.
// (5,6) timer0 1kHz; (9,10) timer1 500Hz; (3,11) timer2 500Hz
#define PIN_OUTPUT1 11  // Ch. 2 L-cooling Fan
#define PIN_OUTPUT0  5  // Ch. 1 Heater
#define PIN_OUTPUT2  3  // Ch. 3 PWM of high freq. at 2.5kHz to drive 4-pins cooling fan
#define PIN_OUTPUT3  6  // Ch. 4 for Peltier cooling 

#define PIN_OUTPUT9  9  // H-bridge VHS2SP30 (disable temporary)
// LED on for warning when sensor is out of range
#define PIN_OUTPUT12  4 // RED LED indicator to warn overheating 
#define PIN_OUTPUT13 A3 // Amber LED (= Internal Arduino LED) indicator to show preheating
#define PIN_INPUT2 2    // Control pin for Pre-heating (Switch preheating to main modes manually) 
#define num 5           // Sampling number for average thermistor 
// PIN D10, 12, 13 were reserved to ADC MCP3550 for high precision 

#define CLK_PIN     8 //8  //12  S1 // Endoder pins: Circular encoder (G|S1|S2|SW|Vcc)
#define DAT_PIN     7 //9  //11  S2 //
#define SWITCH_PIN A2 //10 //10  SW // Only A0-A5 can be converted to digital pins, not A6,A7 

byte  leftCursor[8] = {B00000, B00000, B00100, B01000, B11111, B01000, B00100, B00000}; // L-arrow: <-
byte rightCursor[8] = {B00000, B00000, B00100, B00010, B11111, B00010, B00100, B00000}; // R-arrow: ->
byte     Celcius[8] = {B11100, B10100, B11100, B00000, B00000, B00000, B00000, B00000}; // oC

char * menuItems[] = {"T1", "T2", "T3",  "t1", "t2", "t3"}; // exclude pre-, post-, and 1st extended segments
//int * p[] = {-1, 0, 4, 8, 12};
int menuNum = sizeof(menuItems)/sizeof(char *); // array size
int menuStep = 0;  // number of menu pages
int itemStep = 0;  // number of setting items
int menuOut = 0;
bool idummy = true;// to avoid when initial value of encoder is not zero  
int k = 1000;      // unit prefix ex.) 1 s = 1 ms * k

Bounce debouncer = Bounce();

//Input power control
int pmax = 255;       // max. power; usually, 255
int pmax_fan = 255;   // max. power for H- and L-Fans 
int pmax_Pcool = 255; // max. power for Peltier cooler
int pmin = 50;        // 25; min. power for idle running of PWM H-FAN
                      // P_min = 20 (I_min=0.006A, I_max=1.400A) for Model: MGT4012XB-W28

double dT  = 1.0;     // max power unless Tc0 (current T) < (setpoint T - delta T)
double dT0 = 0.3;     // pre-heating segment          
double dT1 = 1.05;    //0.5;    // T range of supressed power
double dT2 = 0.3;     //double dT2 = 2.0;
double dT3 = 4.5;
double dT4 = 6.30;    // annealing segment (segment 4)
double dT5 = 6.0;

double  rP  = 0.05;   // reduce power factor
double  rP0 = 0.30;   // reduce power factor for pre-heating segment 
double  rP1 = 0.10;  //0.02;   // reduce power factor for heating ramp (segment 1)  <== since Unit 10s_A heating rate is too high
double  rP2 = 0.30;   // reduce power factor for isothermal denaturation (segment 2)
double  rP4 = 3.00;   // reduce power factor for isothermal denaturation (segment 4)
double  rP5 = 0.10;  //0.3   0.4 0.08;   // reduce power factor for heating ramp (segment 5)
double  rP6 = 0.50;   //0.5 reduce power factor for isothermal extension (segment 6, Post-heating)

double pow2 = 160;   // Disable
double pow4 =   5;   // constant heating during annealing

// BATERY (LiFePO4, 12.8V, 3.3Ah; 8A BMS; DMBP-LF128-4S1P-B8)
//double dTh1 = 0.0; double dTh2 = 0.0; double dTh3 = 0.0; // Heating ramp 1 calibration for Cycle 1, 2, 3 
//double dTc1 = 0.0; double dTc2 = 0.0; double dTc3 = 0.0; // Heating ramp 2 calibration for Cycle 1, 2, 3

  
// PWM freq. of (Uno, Nano, Mini) Pins: (5,6: timer0 = 980Hz); (9,10: timer1 = 490Hz); (3,11: timer2 = 490Hz),  
// Increasing D3 frequency (500Hz -> 2.5kHz) using PWM.h library for H-cooling fan  
int fan = PIN_OUTPUT2;    // fan = D3; succeded freq.: Pin 3, 9, 10 (5 is only with time reset, but cannot be 6, 11)
int32_t frequency = 2500; // D3 frequency (Hz) <- 2.5kHz, cf.) 25000 = 25kHz
// int fan_power = 0;                           

float Outputz0, Outputz1, Outputz2, Outputz3;   
 long *Pn = NULL;  // To handle the count number for LCD display
  int *Pm = NULL;  // To handle the cycle number for idle looping after completed cycles
  int jj = 1;      // Counter for Excel

/* Timer setting for segment control
   Assign time interval delta_t: Duration of heating, denatation, cooling and annealing/extension  
*/
//[** H-Ramp//-- Denaturation --\C-Ramp\\\\--Annealing--//H-Ramp/--Extension--]************ unit: second *******
// Assume Max. PCR time is less than 5h.                                                                      **
// ex.) 5h = 18 Mms = 0.018 Gms < long integer limit (2.1 G) --> long integer is sufficient.                  **
int mx = 30;   // Set total number of cycles                                                                  **
long tt1=  180;                            // Extension denaturation time only for 1st cycle                  **
long t1 = 25; long t2 = 30;                // Denaturation time: H-Ramp + isothermal                          **
long t3 = 20; long t4 = 30;                // Annealing time: C-Ramp + isothermal                             **
long t5 =  8; long t6 = 30;                // Extension time: H-Ramp + isothermal                             **
long  p =  1; long pf = 300;               // Post heating time for last extension of last cycle              **

long ta, tb, tc, td, te, tf = 0;           // t_a-f are the time duration for each segment                    **
long Tcycl = t1 + t2 + t3 + t4 + t5 + t6;  // T_cycle: period of a cycle                                      **

long nf = mx * Tcycl + tt1;                // Extend total PCR time for tt1                                   **
int flag = mx;                             // Flag for idle running Arduino after the end of cycles           **
//**************************************************************************************************************

unsigned long Time0, preTime, nowTime; 
long cnt = 0;       // count time
bool tflag = true;  // time flag
int pre_m = 0;      // index for each cycle start

/* -------  Thermistor & Temperature ----------------------------------------------    */
double Trt = 10.0;  // Set r.t. = 30 oC for safety in accident of sensors taken off   
                    // -273 oC when disconnected 
                    //  r.t.   when taken off      

double Tc0, Tc1, Tc2, Tc3; //  Use only Tc0, disable others. 

void Temperature(double *, double *, double *, double *);

void LcdDisplay(int, int, double *, double *);

//void Serial_print(int *, double *, int *, int *);

// ---------------------------------------------------------------------------------
double Setpoint0, Input0, Output0;             // PID for Ch. 1 
//double Setpoint1, Input1, Output1;             // PID for Ch. 2 
double Setpoint2, Input2, Output2;             // PID for Ch. 3 
double Setpoint3, Input3, Output3;             // PID for Ch. 4 
double sp0, sp2, sp3; // sp1, sp4;

// Setting PID parameters: Kp, Ki, Kd for 4-ch. temperature control (0: for Heating; 1,2,3 for cooling) 
double Kp0= 5, Ki0= 0.3, Kd0= 5;   // Tuning PID parameters for heater heating
//double Kp1=10, Ki1=0.25, Kd1= 5;   // Tuning PID parameters for L-fan cooling & bent the air flow (top, front --> back)
double Kp2= 5, Ki2= 0.4, Kd2=10;   // Tuning PID parameters for PWM H-fan cooling
double Kp3= 5, Ki3= 0.4, Kd3=10;   // Tuning PID parameters for Peltier cooling

PID myPID0(&Input0, &Output0, &Setpoint0, Kp0, Ki0, Kd0, DIRECT);  // PID object 0 for heating
//PID myPID1(&Input1, &Output1, &Setpoint1, Kp1, Ki1, Kd1, DIRECT);  // PID object 1 for  ???  (currently disable)
PID myPID2(&Input2, &Output2, &Setpoint2, Kp2, Ki2, Kd2, REVERSE); // PID object 2 H-, L-fans cooling
PID myPID3(&Input3, &Output3, &Setpoint3, Kp3, Ki3, Kd3, REVERSE); // PID object 3 Peltier cooling

// Display                    
LiquidCrystal_I2C lcd(0x27, 16, 2);      // Set address (0x3F): I2C 16x2 LCD
//LiquidCrystal lcd(12, 11, 5, 4, 3, 2);


// ======================================================================
void setup() {

//**************<< Target temperature (Cesius Degree)>>*********************************************  
// in Celsius temperature                                                                         **
  Setpoint0 =  95.0; sp0 = Setpoint0; //sp0 --> Ch. 1: Heater for denaturation                    **
  Setpoint2 =  55.0; sp2 = Setpoint2; //sp2 --> Ch. 2, 3: Cooling fan for annealing               **
  Setpoint3 =  72.0; sp3 = Setpoint3; //sp3 --> Ch. 4: (3-steps PCR) Heater for extension         **
//Setpoint1 =  95.0; sp1 = Setpoint1; //sp1          : Currently disable                          **
//Setpoint4 =  68.0; sp4 = Setpoint4; //Post-heating <-- Usually it is for extension: sp4 = sp3   ** 
//************************************************************************************************** 

Serial.begin(9600); // Initilize serial commucation w/ bound rae: 9600, ..., 115200
// Excel: take data aquisition and plot realtime graph by using PLX DAQ v2
Serial.println("CLEARDATA"); // clears sheet starting at row 2
Serial.println("LABEL, Date,Time,Timer,millis, Counter, SV, Temperature, Output0, pmax_fan, Cycle");

// Assign in/out functions to the pins  
  pinMode(PIN_OUTPUT0, OUTPUT);  pinMode(PIN_OUTPUT1, OUTPUT);  // Ch. 1 ~  Ch. 4
  pinMode(PIN_OUTPUT2, OUTPUT);  pinMode(PIN_OUTPUT3, OUTPUT);  //
  
  pinMode(PIN_OUTPUT9, OUTPUT);                                 // disable temporarly
  pinMode(PIN_OUTPUT12, OUTPUT); pinMode(PIN_OUTPUT13, OUTPUT); // Red and Amber LEDs
  pinMode(PIN_INPUT2, INPUT);                                   // Pre-heating S/W

// encoder pins
  pinMode(CLK_PIN, INPUT);
  pinMode(DAT_PIN, INPUT);
  pinMode(SWITCH_PIN, INPUT_PULLUP);

 // attachInterrupt(digitalPinToInterrupt(PIN_INPUT2),Preheating,LOW);

  lcd.init();        // I2C LCD: initialize 
  lcd.backlight();   // I2C LCD backlight on
  lcd.clear();       // clear LCD
  lcd.begin(16, 2);  // Initialize interface

  lcd.createChar(0, leftCursor);
  lcd.createChar(1, rightCursor);
  lcd.createChar(2, Celcius);

// Encoder w/ bounce2 library
                                // CLK, DAT pins ? 
  debouncer.attach(SWITCH_PIN); // Button pin
  debouncer.interval(5);        // interval in ms

    if (idummy = true) {   // initialize the value of encoder to zero 
       int dSlot = 0;
       idummy = false;
    }
  
  lcd.setCursor(0,0); lcd.print("*** Bio-PCR1 ***");
  lcd.setCursor(0,1); lcd.print("*KW-SG U. KEITI*");
   delay(1000);
  lcd.setCursor(0,0); lcd.print("Model No.:      ");
  lcd.setCursor(0,1); lcd.print("  Unit15s_Pel3_B");
   delay(1000);

// interative input menu ----------------------------------------
  while(menuStep != 99) {

  debouncer.update();               // Update the Bounce instance
  if(debouncer.fell()) menuStep++;  // Pushing number of button

          if (menuStep == 0) displayLogo();               //  No button  
     else if (menuStep == 1) {lcd.clear(); menuStep = 2;} // 1st button to erase display
     else if (menuStep == 2) displayMenu();               // 2nd button
     else if (menuStep == 3) displaySet0();               // 3rd button
     else if (menuStep == 99) {
        lcd.clear();
        lcd.println("Here is menu!!!");
        delay(2000);
        menuStep == 99; 
      }
     else  displaySet(); 
  }


    lcd.noCursor();
    lcd.clear();
    lcd.setCursor(0,0); lcd.println("> Check Pre-heat");
    lcd.setCursor(0,1); lcd.println("> PCR ready...  ");
    delay(3000);
//---------------------------------------------------------------


//turn the PID on
  myPID0.SetMode(AUTOMATIC);           // Automatic
  myPID0.SetTunings(Kp0,Ki0,Kd0);      // Tunings

  //myPID1.SetMode(AUTOMATIC);           // Automatic // Diable
  //myPID1.SetTunings(Kp1,Ki1,Kd1);      // Tunings

  myPID2.SetMode(AUTOMATIC);           // Automatic
  myPID2.SetTunings(Kp2,Ki2,Kd2);      // Tunings

  myPID3.SetMode(AUTOMATIC);           // Automatic
  myPID3.SetTunings(Kp3,Ki3,Kd3);      // Tunings

//initialize all timers except for 0, to save time keeping functions
InitTimersSafe();
//H-Fan frequency: sets the frequency for the specified pin 
bool success = SetPinFrequencySafe(fan, frequency);

#ifndef ESP8266
while (!Serial); // will pause Zero, Leonardo, etc until serial console opens
#endif

//Display info. when the pin frequency was set successfully
  if(success) {
     lcd.setCursor(0,0);
     lcd.print("For h-speed fan:");
     lcd.setCursor(0,1);
     lcd.print("Modified freq=2.5kHz") ;
     delay(1000);
     lcd.clear();
  }


}
  
// =========================================================================
void loop() {

/* Preheating phase was introduced in order to enhance the initial stability 
 * of 1st PCR cycle especially. Task of this preheating phase is: 
 * 1) to provide the same temperature to the end of the annealing temperature 
 * (T = sp2) before PCR cycle starting, so that the initial start will be 
 * similar to the starting temperature of other cycles and
 * 2) to warm the heat chamber.
*/

// Switching Preheating/PCR main cycles ************************************ 
/* This function is for preheating Bio-PCR                                */
// ***** Switching mode w/ pin D2 ******************************************

 if (digitalRead(PIN_INPUT2) == 1){           // Pull-down switch

  // **********************(( Preheating)) *********************************
    digitalWrite(PIN_OUTPUT13, HIGH);  // S/W on (True, 1) -> 5V <== Preheating ON
 
// Temperature Calc ---------------------------------------------------

    Temperature(&Tc0, &Tc1, &Tc2, &Tc3); // Currently use only Tc0  and Tc1 to Tc3 were disable 

// --------------- PID Inputs to calculate Outputs---------------------
  Input0 = Tc0;       // T: Heater
  myPID0.Compute();

     Output0 = map(Output0, 0,255, 0,pmax); // mapping Output in ordet to limit the power

//------------- Send PID outputs to PWM on analogWrite(pin no.) -----------

// initialization of all of Ch.'s
 analogWrite(PIN_OUTPUT0, 0);        // OFF Ch. 1: Heater off
 analogWrite(PIN_OUTPUT1, 0);        // OFF Ch. 2: L-fan off
 pwmWrite(fan, 0);                   // OFF Ch. 3: H-Fan off
 analogWrite(PIN_OUTPUT3, 0);        // OFF Ch. 4: Peltier cooling off  

// .............. for pre-heating ...........................................................
//  Set SP = sp3 

  if((Tc0 - sp3) >= 0){                   // high filter clipping out 
      Setpoint0 =  sp3;                   // 
      analogWrite(PIN_OUTPUT0, 0);        // to supress overshoot compulsively
  } 

  else if (sp3 - Tc0 <= dT0){             // When dT =< 5, reduce heating power
      Setpoint0 =  sp3;
      analogWrite(PIN_OUTPUT0, Output0*rP0); // Ch. 1: Reduced heating power mode

  } 

  else { 
  Setpoint0 =  sp3;                         //ON  Ch. 1: Heater heating on  
  analogWrite(PIN_OUTPUT0, Output0);  

  }

// Serial monitoring -----------------------
 /* Serial.print(Input0, 2); Serial.print(", "); Serial.print(Input1, 2); Serial.print(" "); 
  Serial.println(" "); */

// cycle = 0, loop count n = -999 
 int  m, m0 = 0; //long n = -999; // cycle No. of preheaing: m = 0, m0 is a dummy parameter. 
   if (tflag == true) {
     Time0 = millis();
     //lcd.clear();  
     tflag = false;
   }
     nowTime = millis();
     preTime = (nowTime - Time0);  // prints time since for-loop started
     cnt = preTime;                // cnt is second (s), not looping number (ns) 


float ssp = Setpoint0;         
if (ssp >= 100){ssp = 100;}        // Assign max. 100 oC to the noise which occures when switching pre to norm heating 
                                   // This noise may create a impulse peak on the serial monitoring graph.

// Save and Display data with Excel:  Using PLX DAQ v2
Serial.print("DATA,DATE,TIME,TIMER,");
Serial.print(millis()); Serial.print(",");
Serial.print(jj++); Serial.print(",");
Serial.print(ssp); Serial.print(",");
Serial.print(Tc0); Serial.print(",");
Serial.print(Output0); Serial.print(",");
Serial.print(pmax_fan); Serial.print(",");
Serial.println(m); 
// Serial.print(","); Serial.println("AUTOSCROLL_20");

/*
 Serial.print(ssp); Serial.print(", ");
 Serial.print(Tc0); Serial.print(", ");
 Serial.print(Output0); Serial.print(", ");
 Serial.print(pmax_fan); Serial.println(" ");
*/

// LED display -----------------------------
 LcdDisplayPreHtng(m, cnt, &Setpoint0, &Tc0);
   
  }  // End of pre-heating

  else {
// *******************(( PCR main cycles ))*****************************************************
    digitalWrite(PIN_OUTPUT13, LOW); // S/W off(0) -> 0V -> False state 0  0 <== Preheating OFF
    lcd.init();        // I2C LCD: initialize 
    lcd.clear();       // clear LCD
//..............................................................................................

//convert seconds to milliseconds
// ex.) 5h = 18 Mms = 0.018 Gms < long integer limit (2.1 G) --> long integer is sufficient.
tt1 = tt1*k; 
t1 = t1*k; t2 = t2*k; t3 = t3*k; t4 = t4*k; t5 = t5*k; t6 = t6*k; 
Tcycl = t1 + t2 + t3 + t4 + t5 + t6;  // T_cycle: period of a cycle   
nf = mx * Tcycl + tt1;        // Extend total PCR time for tt1 --> calc. it again with new mx
flag = mx;                    // Since cycle number changed, flag must be changed. 
pf = pf*k;

 // Serial.print(t1);Serial.print(", ");
 // Serial.print(Tcycl);Serial.print(", "); Serial.println(nf);

Time0 = millis();

// Now, start the periodic thermocycle w/ for-loop statement
//
for (long n = 1; n < nf; n++) { // T_running time = cycle number * cycle period + added tt1
//for (int n = -tt1 + 1; n < nf; n++){ // T_running time = cycle number * cycle period + added tt1
                                     // Shift n in -ttl seconds: ex.) (-19, ..., 0,) 1, 2, 3, ...  
                                     // Note: Zero is added to count number.
 
 digitalWrite(PIN_OUTPUT13, LOW); // S/W off(0) -> 0V -> False state 0 <== Preheating over

/*                                    
int preTime =  millis()/1000;  // Display time in second since program started
cnt++;  // count number: It starts at zero. 
*/
     nowTime = millis();
     preTime = (nowTime - Time0);  // Count the elapsed time since for-loop started
     cnt = preTime;                // cnt is in milisecond (ms), not looping number (ns) 

  Pn = &n;                         // Pointer to handle total cycle number

     long cnt1 = cnt - tt1; 
      int  m = cnt1/Tcycl + 1;    // calc. cycle number m, quetient  = dividend / divisor 
     long m0 = cnt1%Tcycl;        //                       remainder = dividend % divisor  
  
        if (cnt1 <= 0){           // set m = 1 for negartive cnt1
            m = 1;                // since the negative cnt1 mest be included to entended denaturation only in 1th cycle.
       }

  Pm = &m;

      int now_m = m;


double ssp = Setpoint0;

//Serial.print(Outputz0);Serial.print(", ");
// PLX-DAQ-v2 serial transfer for Excel file
Serial.print("DATA,DATE,TIME,TIMER,");
Serial.print(millis()); Serial.print(",");
Serial.print(jj++); Serial.print(",");
Serial.print(ssp); Serial.print(",");
Serial.print(Tc0); Serial.print(",");
Serial.print(Output0); Serial.print(",");
Serial.print(pmax_fan); Serial.print(",");
Serial.println(m); 
// Serial.print(","); Serial.println("AUTOSCROLL_20");

// For Arduino sirial plotter ---------------------- 
 Serial.print(ssp);Serial.print(", ");   
 Serial.print(Tc0);Serial.print(",  ");  
 Serial.print(Output0);Serial.print(", ");
 Serial.print(pmax_fan);Serial.println(", ");

 //Serial.print(m);Serial.print(", ");
 //Serial.print(m0);Serial.print(", ");Serial.println(nf);
 
  if (cnt > nf) {
    break;
  }                // exit on the end of normal PCR cycles

 
////////////////////////////////////////////////////////////////////////////////////////////////////

// Calculate segment times before each cycle starts
  //if (m <= 2 || m0 == 0){   // if (m <= 1 || m0 == 0){
//  if (m <= 1 || m0 <= 100){

    // ta = (m-1)*Tcycl + t1; // Starting time for segment a: Clac. ta's each cycle at either m <=1 or m0=0 
    // ----- calc. the extend tb for 1st longer denatuation ----------------------------------------------------
       if (m == 1 && now_m != pre_m){         // Extended denaturation in only Cyle #1 
       //if (m == 1 && m0 <= 100){            // Extended denaturation in only Cyle #1 
        // ta = (m-1)*Tcycl + t1;             // for segment a
          ta = t1; 
          tb = ta + t2 + tt1;                 // for segment b (extend tb +tt1 in only Cycle #1)
          pre_m = now_m;
       }
       else if (m >= 2 && now_m != pre_m){    // Since Cycle #2 
       //else if (m >= 2 && m0 <= 100){       // Since Cycle #2 
          ta = (m-1)*Tcycl + t1 + tt1;        // for segment a (shift the starting time +tt1 after Cyle #2)
          tb = ta + t2;                       // for segment b 
          pre_m = now_m;
       }
       else{

       }
      
    // -----------------------------------------------------------------------------------------------
         tc = tb + t3;   // for segment c       
         td = tc + t4;   // for segment d
         te = td + t5;   // for segment e
         tf = te + t6;   // for segment f

/*  Time parameters for each segments........................
             ____t2___
            /         \
         t1/           \                       tcycl
          /             \t3            ___t6___  
                         \            /
                          \          /t5 
                           \___t4___/
    -tt1     ta       tb    tc      td te      tf
 Segments: (1     2)   (3       4)   (5   6) 
 Phases: Denaturation   Anneling     Extension
*/  
////////// Temperature Calc /////////////////////////////////

    Temperature(&Tc0, &Tc1, &Tc2, &Tc3);

// --------------- PID Inputs to calculate Outputs-----------

  Input0 = Tc0;       // T for Heater heating
  myPID0.Compute();
    
 // Input1 = Tc1;     // Diable 
 // myPID1.Compute();

  Input2 = Tc2;      // T for H-, L-fans dooling (Sychronized T3 => T1)
  myPID2.Compute(); 

  Input3 = Tc3;      // T for Peltier cooling
  myPID3.Compute();
 
// --------- Set null output when sensor is disconnected ------
// To protect from the acciential overheat caused by sensor broken, 
// turn on a red LED indicator and turn off heating power supply.  
// i.e.: Sensor broken (Tc0 = -273 oC), Ambient room temperature (Trt = 25 oC) 
// Currently, set the warning signal disable. Red LED is used just an indicator for the normal operation

  digitalWrite(PIN_OUTPUT12, LOW); // Red LED on during normal operating time
                                   //(usually over room temperature: Tc0 > Trt ) 
  if (Tc0 > Trt) {
    //Output0 = 0; 
    digitalWrite(PIN_OUTPUT12, HIGH); // LED on for warning of heating 
  }

//------------- Send PID outputs to PWM on analogWrite pins ---------------
// initialization of all of Ch.'s by sending zero PWM power signal
 analogWrite(PIN_OUTPUT0, 0);        // OFF Ch. 1 for Heater
 analogWrite(PIN_OUTPUT1, 0);        // OFF Ch. 2 for L-fan
 pwmWrite(fan, 0);                   // OFF Ch. 3 for H-fan
 analogWrite(PIN_OUTPUT3, 0);        // OFF Ch. 4 for Peltier cooling

/* Notes:
   Three phases for PCR is divided to five segments. Two PID scheme are possible:  
     1) Mode I: 5-segments independently. This mode is to supress and reduce the overshot by both coding and PID parameters. 
     2) Mode II: A pair of segments combined to make three phases: (1+2), (3+4), (5+6) 
        for denaturation, annealing and extension, respectively. This mode is relying only on PID parameters.
   Currently, we selected Mode I.
*/ 

if(cnt <= ta){                        //---------- segment 1 ---(Heating ramp1 for Denaturation)-- 

  pwmWrite(fan, 0);                      // Ch. 3: H-fan off 
  analogWrite(PIN_OUTPUT3, 0);           // Ch. 4: Peltier cooling off
  analogWrite(PIN_OUTPUT1, 0);           // Ch. 2: L-fan off

     Setpoint0 =  sp0;                   // Ch. 1: Heater ON 
     analogWrite(PIN_OUTPUT0, Output0);  // 

}
else if(cnt > ta && cnt <= tb){       //---------- segment 2 ---(Isothermal heating 1 for Denaturation)-----

     Setpoint0 =  sp0;                   // Ch. 1: Heater on  
     analogWrite(PIN_OUTPUT0, Output0);  //*rP2); //*rP2);   
     analogWrite(PIN_OUTPUT1, 0);        // Ch. 2: L-fan off

// H-fan has time constant about 10 s. 
// So it needs the pre-idling spinning in the minmum rpm before starting. 
    if ((tb - cnt) <= 10*k){
       pwmWrite(fan, pmin);              // Turn on PWM H-fan for pre-idle running (PWM_min = 20)
    // pwmWrite(fan, pmax_fan); 
    }                            

}
else if(cnt > tb && cnt <= tc){       //---------- segment 3 --(Cooling ramp 1 for Annealing)-----------
  analogWrite(PIN_OUTPUT0, 0);            // Ch. 1: heater OFF
  //analogWrite(PIN_OUTPUT1, 0);          //  

   if ((Tc0 - sp2) > dT3){                // Unless dT =< 5, keep max heating power at 255
      Setpoint0 =  sp2;
      Setpoint2 =  sp2; 
      pwmWrite(fan, pmax_fan);            // Ch. 3: H-fan max (max H-fan cooling)
      analogWrite(PIN_OUTPUT1, pmax_fan); // Ch. 2: L-fan max
      analogWrite(PIN_OUTPUT3, Output3);  // Ch. 4: Peltier cooling ON
   }

   else{
/*
        switch (m) {
           case 1:
              sp2 = sp2 - 3; // since first cooling is always little higher than others 
              break;
        }
*/    
      Setpoint0 =  sp2;                   // Disable Setpoint0 in order to display sp2 on LCD 
      Setpoint2 =  sp2;                   // Ch. 2, 3, 4: ON for cooling
//     pwmWrite(fan, Output2);            // Fan_1 on: ON Ch. 3 (on H-cooling)

      pwmWrite(fan, Output2); //pmax_fan);// Ch. 3: H-fan PID
      analogWrite(PIN_OUTPUT1, Output2);  // Ch. 2: L-fan ON
      analogWrite(PIN_OUTPUT3, Output3);  // Ch. 4: Peltier cooling ON
   }

}
else if(cnt > tc && cnt <= td){       //---------- segment 4 ---(Isothermal heating 2 for Annealing)------

//  pwmWrite(fan, 0);                     // Fan_1 off: OFF Ch. 3 (off H-cooling)
  pwmWrite(fan, pmin); //Output2); // 0); // Ch. 3 H-fan pmin for cooling of Peltier heat sink
  analogWrite(PIN_OUTPUT1, Output2);      // Ch. 2: L-fan on for ventilation
  analogWrite(PIN_OUTPUT3, 0); //Output3);// Ch. 4: Peltier cooling OFF
 
  Setpoint0 =  sp2;                       // Ch. 1: Heater  
  
  if((Tc0 - sp2) > dT4){                  // high filter clipping out 
     Setpoint0 =  sp2;     
     analogWrite(PIN_OUTPUT0, 0);         // to supress overshoot especially in annealing heating!!!
     analogWrite(PIN_OUTPUT3, Output3);   //*rP4p);  // Ch. 4: Peltier cooling ON
     pwmWrite(fan, Output2);              //*rP4p);  // 0); //pmax_fan);           // Ch. 4: H-fan PID 
     analogWrite(PIN_OUTPUT1, Output2);   //Output2); //*rP4p); //Output2); //0);  // Ch. 2: L-fan PID  
  }

  else if ((sp2 - Tc0) >= 0) { //dT4) {  //0)  {   // low filter clipping out 
     pwmWrite(fan, pmin*2/3); // 0);  pmin); //pmax_fan);                        // Ch. 4: H-fan ON 
     analogWrite(PIN_OUTPUT1, Output2/3); //pmax_fan); //Output2*rP4p);          // Ch. 2: L-fan (1/3) ON
     analogWrite(PIN_OUTPUT0, Output0*rP4); //*rP4); //pow4);                    // Ch. 1: Heater ON w/ *rP4
  }

}
if(cnt > td && cnt <= te){            //---------- segment 5 ---(Heating ramp 2 for Extension)----------- 
  pwmWrite(fan, 0);                   // Ch. 3: H-fan off 
  analogWrite(PIN_OUTPUT1, 0);        // Ch. 2: L-fan OFF
  analogWrite(PIN_OUTPUT3, 0);        // Ch. 4: Peltier cooling OFF

      Setpoint0 =  sp3;
      analogWrite(PIN_OUTPUT0, Output0); //*rP5);     // Ch. 1: Heater ON w/ *rp5
 
}

else if(cnt > te && cnt <= tf){       //---------- segment 6 ---(Isothermal heating 3 for Extension)---- 
  pwmWrite(fan, 0);                     // Ch. 3: H-fan off
  analogWrite(PIN_OUTPUT1, 0);          // Ch. 2: L-fan off
  analogWrite(PIN_OUTPUT3, 0);          // Ch. 4: Peltier cooling off

  Setpoint0 =  sp3;                     // Disable Setpoint0 in order to display sp3 on LCD 
  analogWrite(PIN_OUTPUT0, Output0);    // Ch. 1: Heater ON     

}

else{
}     


//--------------------((Display LCD))----------------------------------------

  LcdDisplay(m, cnt, &Setpoint0, &Tc0);
  
//---------------------------------------------------------------------------

     if (cnt >= nf) {
        tflag = true;       
        break;
     }                 // exit on the end of normal PCR cycles


}  // end of for-loop
   

/* End of PCR ==> turn off Ch. 4, 2 */
// infinite loop
 
 tflag = true; 
 while(flag >= mx) { 
 
// Post-heating segment ================================================================

  // tflag, timer and LCD reset for post-heating segment
   if (tflag == true) {
     Time0 = millis();                  // Reset timer
     lcd.clear();
   }

   while (p <= pf && tflag == true ){   // Post-heating segment
   p++;
  
     nowTime = millis();
     preTime = (nowTime - Time0);      // prints time since for-loop started
     cnt = preTime;                    // cnt is second (s), not looping number (ns) 

   // Temperature Calc -------------------------------------
       Temperature(&Tc0, &Tc1, &Tc2, &Tc3);
   // PID Inputs to calculate Outputs-----------------------
      Input0 = Tc0;                    // T of Heater

  //--------------------------------------------------------
  
    if((Tc0 - sp3) >= 0){                 // high filter clipping out 
       Setpoint0 =  sp3;                  // Keep T_extension for post-heating  
       analogWrite(PIN_OUTPUT0, 0);       // to supress overshoot 
    } 
    else{
       Setpoint0 =  sp3;                  // Ch. 1: Heater on 
       analogWrite(PIN_OUTPUT0, Output0); //*rP6); // 
       analogWrite(PIN_OUTPUT1, 0);       // Ch. 2: L-fan off
       //analogWrite(PIN_OUTPUT1, Output1); // *rP6);  
    }
   // LED display -----------------------------
     LcdDisplayPostHtng(mx, cnt, &Setpoint0, &Tc0);

    unsigned long m0 = 0;
    float ssp = Setpoint0;

// Save and Display data with Excel:  Using PLX DAQ v2
Serial.print("DATA,DATE,TIME,TIMER,");
Serial.print(millis()); Serial.print(",");
Serial.print(jj++); Serial.print(",");
Serial.print(ssp); Serial.print(",");
Serial.print(Tc0); Serial.print(",");
Serial.print(Output0); Serial.print(",");
Serial.print(pmax_fan); Serial.print(",");
Serial.println(m0); 
// Serial.print(","); Serial.println("AUTOSCROLL_20");

    Serial.print(ssp);Serial.print(", ");
    Serial.print(Tc0);Serial.print(", ");  
    Serial.print(Output0);Serial.print(", ");
    Serial.print(pmax_fan);Serial.println(" ");
    //Serial.print(mx);Serial.print(", ");
    //Serial.print(m0);Serial.print(", ");Serial.println(nf);
 
     if (cnt > pf) {
        tflag = false;
        break;
     }                // exit on the end of normal PCR cycles

   } // end of inner while
//================================================================================

// unlimit looping starts ---------------------------(( PCR COMPLETE))------------  
      analogWrite(PIN_OUTPUT0, 0);  // Ch. 1: OFF 
      analogWrite(PIN_OUTPUT1, 0);  // Ch. 2: OFF
      pwmWrite(fan, 0);             // Ch. 3: OFF
      analogWrite(PIN_OUTPUT3, 0);  // Ch. 4: OFF
  
////////// Temperature Calc /////////////////////////////////

    Temperature(&Tc0, &Tc1, &Tc2, &Tc3);

  // LCD display ---------------------
  
  //LcdDisplay(m, n, &Setpoint0, &Tc0);

   
     lcd.clear();       // clear LCD
     lcd.setCursor(0,0);
     lcd.print("Complete PCR");

     lcd.setCursor(13,0);
     lcd.print(mx);
     lcd.print("c");
   
     lcd.setCursor(0,1); 
     lcd.print("PV:"); lcd.print(Tc0, 1); lcd.write(byte(2)); 

     lcd.setCursor(9,1);                   // Col 10, Line 1
     lcd.print("t:");  lcd.print(nf/1000); // lcd.print("N:");  lcd.print(*Pn);   
     lcd.print("s");

      digitalWrite(PIN_OUTPUT12, HIGH);    // Blink red LED
      delay(500);
      digitalWrite(PIN_OUTPUT12, LOW);
      delay(500);     

    // delay(1000);   

/*
// Save and Display data with Excel:  Using PLX DAQ v2
Serial.print("DATA,DATE,TIME,TIMER,");
Serial.print(millis()); Serial.print(",");
Serial.print(jj++); Serial.print(",");
Serial.print(ssp); Serial.print(",");
Serial.print(Tc0); Serial.print(",");
Serial.print(Output0); Serial.print(",");
Serial.print(pmax_fan); Serial.print(",");
Serial.println(m0); 
// Serial.print(","); Serial.println("AUTOSCROLL_20");
*/

    unsigned long m0 = 0;
    float ssp = Setpoint0;
    Serial.print(ssp);Serial.print(", ");
    Serial.print(Tc0);Serial.print(", "); 
    Serial.print(Output0);Serial.print(", ");
    Serial.print(pmax_fan);Serial.println(" ");
    //Serial.print(mx);Serial.print(", ");
    //Serial.print(m0);Serial.print(", ");Serial.println(nf);


   } // end of outer while
  }  // end of else in 1st if statement  
}    // end of loop() ================(( End of loop ))========================


void Temperature(double *Tc0, double *Tc1, double *Tc2, double *Tc3) {

// Thermistor parameters ---------------------------------------------------------
// This function is for 4-Ch. However, currently only one thermistor (*Tc0) was used, and so
// *Tc1 to *Tc3 were disable. 
int ThermistorPin0 = 0; //int ThermistorPin1 = 1; int ThermistorPin2 = 2; int ThermistorPin3 = 3;
int Vp0[num]; //, Vo1, Vo2, Vo3;  // Vp1[num], Vp2[num], Vp3[num];
double avg_Vo0; //, aver_Vo1, aver_vo2, aver_Vo3;

//NOTE: R0's must be replaced by real measured values for the better precision.  
// using R0 = 10 kOhm at r.t. 
double R1 = 10000; //, R3 = 10000, R5 = 10000, R7 = 10000; // Disable Thermistor 2 to 4 
double logR2;      //, logR4, logR6, logR8; // Disable Thermistor 2 to 4 
double    R2;      //,    R4,    R6,    R8;
double    T0;      //,    T1,    T2,    T3; 

// Coefficients of Steinhart?Hart equation ---------------------------------------
// Unit15_Pel3 (A)
//double c1 = 1.078062063e-3,  c2 = 2.348020890e-4, c3 = 1.472346872e-7; // Unit 15_Pel3

// Unit15_Pel3_B 
double c1 = 1.057301892e-3,  c2 = 2.363088481e-4, c3 = 1.546236340e-7; // Unit 15_Pel3
//double c4 = c1, c5 = c2, c6 = c3; // Blue 10k (T1, 50/70/100)
//double c7 = c1, c8 = c2, c9 = c3; //
//double c10= c1, c11= c2, c12= c3; //
           

// Read the voltage (V) of Analog pin
// Read num times
for (int i=0; i < num; i++){
Vp0[i] = analogRead(ThermistorPin0); 
delay(10);
    //Vo0 = analogRead(ThermistorPin0); Vo1 = analogRead(ThermistorPin1);
    //Vo2 = analogRead(ThermistorPin2); Vo3 = analogRead(ThermistorPin3);
}

// Calc. average
avg_Vo0 = 0;
   for (int i=0; i<num; i++){
     avg_Vo0 += Vp0[i];
   } 
avg_Vo0 /= num;

// Convert V to R, using the voltage divider: reference resistor (R1,2,3,4) are pull-down, thermostor (Rx) is pull-up.  
  R2 = R1 / (1023.0/avg_Vo0 - 1); 
  // R4 = R3 / (1023.0/(double)Vo1 - 1.0); // Vout on R1, R3
  // R6 = R5 / (1023.0/(double)Vo2 - 1.0); 
  // R8 = R7 / (1023.0/(double)Vo3 - 1.0); //         R5, R7
 
  logR2 = log(R2); // logR4 = log(R4); logR6 = log(R6); logR8 = log(R8);

// Convert R to T, using Steinhart?Hart equation  
 // Steinhart?Hart equation: T[K] = 1 / (A + B[ln(R)] + C[ln(R)]^3)
  T0 = (1.0 / (c1 + c2*logR2 + c3*logR2*logR2*logR2)); 
  //T1 = (1.0 / (c4 + c5*logR4 + c6*logR4*logR4*logR4));
  //T2 = (1.0 / (c7 + c8*logR6 + c9*logR6*logR6*logR6));
  //T3 = (1.0 / (c10 + c11*logR8 + c12*logR8*logR8*logR8));

// Alternatively, there is B-model: 1/T = 1/T0 + (1/B)ln(R/R0), where T0 = 298.15K, R0 = 10 kOhm 
// Unit conversion: Convert Kelvin to Celsius unit

*Tc0 = T0 - 273.15; // Tc22 = Tc0;
//*Tc1 = T0 - 273.15; 
//*Tc2 = T2 - 273.15;  
//*Tc3 = T3 - 273.15;             

// Assign *Tc0 to *Tc1 to *Tc3, because currently ony one thermistor (Tc0) was used. 
    *Tc1 = *Tc0;     // Sychronized T1 <= T2 
    *Tc2 = *Tc0;     // Sychronized T1 <= T3 
    *Tc3 = *Tc0;     // Sychronized T1 <= T4
}

void LcdDisplayPreHtng(int m, long cnt, double *Setpoint0, double *Tc0) {

  lcd.setCursor(0,0);             // Col 0, Line 0
    lcd.print("SP:");
    lcd.print(*Setpoint0, 1);
    lcd.setCursor(7,0); lcd.write(byte(2)); //lcd.print((char) 223);

  lcd.setCursor(9,0);
  lcd.print("Pre-Htg");

  lcd.setCursor(0,1);  // Col 0, line 1
  lcd.print("PV:");
  lcd.print(*Tc0, 1);
  lcd.setCursor(7,1); lcd.write(byte(2));

  lcd.setCursor(9,1);
  lcd.print("t:");
  lcd.print(cnt/1000);
  lcd.print("s");
  //delay(1000);
  //lcd.clear();         // clear LCD
}

void LcdDisplayPostHtng(int mx, long cnt, double *Setpoint0, double *Tc0) {

  lcd.setCursor(0,0);             // Col 0, Line 0
    lcd.print("SP:");
    lcd.print(*Setpoint0, 1);
    lcd.setCursor(7,0); lcd.write(byte(2));

  lcd.setCursor(9,0);
  lcd.print("Pos-Htg");

  lcd.setCursor(0,1);  // Col 0, line 1
  lcd.print("PV:");
  lcd.print(*Tc0, 1);
  lcd.setCursor(7,1); lcd.write(byte(2));                  

  lcd.setCursor(9,1);
  lcd.print("t:");
  lcd.print(cnt/1000);
  lcd.print("s");
  //delay(1000);
  //lcd.clear();         // clear LCD
  }

void LcdDisplay(int m, long cnt, double *Setpoint0, double *Tc0) {
// Display 4-temp. on LCD
 
//lcd.begin(16, 2);
 
 // Print four Temp.'s to the LCD.
  // display at col 0
  lcd.setCursor(0,0);             // Col 0, Line 0
      lcd.print("SP:");
      lcd.print(*Setpoint0, 1);
        lcd.setCursor(7,0); lcd.write(byte(2));
  lcd.setCursor(0,1);             // Col 0, line 1
      lcd.print("PV:");
      lcd.print(*Tc0, 1);                  
        lcd.setCursor(7,1); lcd.write(byte(2));

  lcd.setCursor(9,0);             // Col 9, Line 0
      lcd.print("Cyl:");
      lcd.print(m, 1);            // *Pm      
      lcd.print("c");                

  lcd.setCursor(9,1);             // Col 10, Line 1
      lcd.print("t:");
      lcd.print(cnt/1000);        // old: lcd.print(n); //preTime, 1);                  
      lcd.print("s");             // Clean up right nonerased pixels  
}

// =================(( Now, all of below are for encoder. ))===================
void displayLogo() {
  lcd.setCursor(0,0); lcd.print("*** Bio-PCR1 ***");
  lcd.setCursor(0,1); lcd.print("*KW-SG U. KEITI*");
}

void displayMenu() {
  lcd.setCursor( 0, 0); lcd.print("Tm: ");
  lcd.setCursor( 0, 1); lcd.print("tm: ");
  for (int i = 1; i <= 3; i++){
  lcd.setCursor(3*i+1, 0); lcd.print(menuItems[i-1]);
  lcd.setCursor(3*i+1, 1); lcd.print(menuItems[i+2]);
  }
  lcd.setCursor(12, 0); lcd.write(byte(2));
  lcd.setCursor(12, 1); lcd.print("s");
  lcd.setCursor(14, 0); lcd.print("Cy");  
  lcd.setCursor(15, 1); lcd.print("c");         
} 

void displaySet0() {
  for (int i = 1; i <= 3; i++){
  lcd.setCursor(3*i+1, 0); lcd.print("--");
  lcd.setCursor(3*i+1, 1); lcd.print("--");
  }
  lcd.setCursor(14,   0); lcd.print("--");

}

void displaySet() {
   lcd.cursor(); 

  switch(itemStep) {
/*    case 1:
      lcd.setCursor(3, 0); lcd.print(" "); 
      if(debouncer.fell()) itemStep++;  
*/    break;
    case 1:
      menuItem1(); 
      if(debouncer.fell()) itemStep = 2;  
    break;
    case 2:
      menuItem2(); 
      if(debouncer.fell()) itemStep = 3;  
    break;
    case 3:
      menuItem3();
      if(debouncer.fell()) itemStep = 4;
    break;
    case 4:
      menuItem4();
      if(debouncer.fell()) itemStep = 5;
    break;
    case 5:
      menuItem5();
      if(debouncer.fell()) itemStep = 6;
    break;
    case 6:
      menuItem6();
      if(debouncer.fell()) itemStep = 7; 
    break;
    case 7:
      menuItem7();
      if(debouncer.fell()) itemStep = 8; 
    break;
    case 8:
      menuItem8();                       // Turn wheel to exit displaySet()
      if(debouncer.fell()) itemStep = 1; 
    break;
    default: 
      itemStep = 1;
    break;
  }
}

void menuItem1() { // set T1 (oC)
  lcd.setCursor(4, 0); lcd.print(int(sp0));
  int dSlot = getEncoderTurn();    // dSlot = (-1, 0, 1)
/*
    if (idummy = 1) {   // initialize the value of encoder to zero 
       dSlot = 0;
       idummy = 2;
    }
 */  
  sp0 = sp0 + dSlot;
    if (sp0 >= 99) {   // cut off last digit when T >= 100; display 100 -> 10  
       lcd.setCursor(6, 0); lcd.print("  ");
    }
}

void menuItem2() { // set T2 (oC)
  lcd.setCursor(7, 0); lcd.print(int(sp2));
  int dSlot = getEncoderTurn();
  sp2 = sp2 + dSlot;
}

void menuItem3() { // set T3 (oC)
  lcd.setCursor(10, 0); lcd.print(int(sp3));
  int dSlot = getEncoderTurn();
  sp3 = sp3 + dSlot;
}

void menuItem4() { // set t1 (ns; ts = ns * 1.14)
  lcd.setCursor(4, 1); 
  if(t2 >= 0 && t2 < 10) lcd.print(0);
  lcd.print(t2);
  int dSlot = getEncoderTurn();
  t2 = t2 + dSlot;  
}

void menuItem5() { // set t2 (ns)
  lcd.setCursor(7, 1); 
  if(t4 >= 0 && t4 < 10) lcd.print(0);
  lcd.print(t4);
  int dSlot = getEncoderTurn();
  t4 = t4 + dSlot;
}

void menuItem6() { // set t3 (ns)
  lcd.setCursor(10, 1); 
  if(t6 >= 0 && t6 < 10) lcd.print(0);
  lcd.print(t6);
  int dSlot = getEncoderTurn();
  t6 = t6 + dSlot;
}

void menuItem7() { // set max. cycles: mx (times)
  lcd.setCursor(14, 0); 
  if(mx < 10) lcd.print(0);
  lcd.print(mx);  // if(c<10)lcd.print(" ");
  int dSlot = getEncoderTurn();
  mx = mx + dSlot;
  if (mx <=0){ mx = 1;} // PCR cycle number >= 1.
  // CAUTION!!!
  // 1) Flag mx must be changed.
  // 2) nf = mx * Tcycl + tt1 must be recalculated.
}

void menuItem8() { // CCW: Repeat menuItem(1~6), CW: Exit menuItem loop  
        lcd.setCursor(15, 1); lcd.write(byte(1));
   int dSlot = getEncoderTurn(); 
      if (dSlot == 0) itemStep = 8;     // wait!
      else if (dSlot == 1) {
         lcd.setCursor(15, 1); lcd.write(byte(0));
        itemStep = 1;                   // CCW   
      }  
      else if (dSlot == -1) {            // CW 
         lcd.setCursor(15, 1); lcd.write(byte(1));
         menuStep = 99;  // 99 = exit flag
         Serial.println("Now exit menuItem");
      }   
      //itemStep = 1; 
}

int getEncoderTurn() {  // returned encoder value: direction = (-1, 0, +1)
  static int oldCLK = LOW;
  static int oldDAT = LOW;
  int direction = 0;

  int newCLK = digitalRead(CLK_PIN);
  int newDAT = digitalRead(DAT_PIN);

//  if (newCLK != oldCLK || newDAT != oldDAT) {  // w/ bouncer.interval(5)
//    if (oldCLK == LOW && newCLK == HIGH) {

  if (newCLK != oldCLK ) {                       // w/ bouncer.interval(50) 
    if (oldCLK == LOW) {

      //direction = -(2*oldDAT - 1); // use DAT as a directional indicator: (CCW, 0, CW)
        direction = 2*oldDAT - 1;    // Since new encoder having D-knob was used, sign was changed!!!!
    }
  }
  oldCLK = newCLK;
  oldDAT = newDAT;
  
  return direction;
}
